# Fritzing sketch schematic (saved by Fritzing 0.9.9b)

parts:
  Part1 = Adafruit 2.7in 400x240 SHARP Memory Display
  MCU1 = Raspberry Pi Zero

nets:
  N1: Part1.3.3V, MCU1.pin_1, MCU1.pin_17
  N2: Part1.GND, MCU1.pin_20, MCU1.pin_25
  N3: Part1.SCLK_5V, MCU1.pin_23
  N4: Part1.SI_5V, MCU1.pin_19
  N5: Part1.SCS_5V, MCU1.pin_31
